// Logisim project Control Unit.circ as structural Verilog
module Control_Unit_2 (
  input  Start,
  input  Fetched,
  input  Halt_Instruction,
  input  Ejecutada,
  input  in_5,
  input  in_6,
  output out_7,
  output CS,
  output out_9
);

  wire Clock, d_ff_1_q, demultiplexer_1_out0, demultiplexer_1_out1, demultiplexer_2_out0,
       demultiplexer_2_out1, demultiplexer_3_out0, demultiplexer_3_out1, demultiplexer_4_out0,
       demultiplexer_4_out1, demultiplexer_5_out0, demultiplexer_5_out1, Reset, undriven, undriven_2;

  D_Flip_Flop d_ff_1 (.clk(Clock), .D(demultiplexer_2_out0), .Q(d_ff_1_q), .preset(Reset));  // open: Qn, en, reset
  Demultiplexer #(.enable("false")) demultiplexer_1 (
    .out0(demultiplexer_1_out0), .out1(demultiplexer_1_out1), .in(demultiplexer_1_out0), .sel(Start));
  Demultiplexer #(.enable("false")) demultiplexer_2 (
    .out0(demultiplexer_2_out0), .out1(demultiplexer_2_out1), .in(d_ff_1_q), .sel(Reset));
  or or_1 (out_7, demultiplexer_3_out0, demultiplexer_5_out1, demultiplexer_1_out1);
  Demultiplexer #(.enable("false")) demultiplexer_3 (
    .out0(demultiplexer_3_out0), .out1(demultiplexer_3_out1), .in(out_7));  // open: sel
  Demultiplexer #(.enable("false")) demultiplexer_4 (
    .out0(demultiplexer_4_out0), .out1(demultiplexer_4_out1), .in(demultiplexer_3_out1),
    .sel(Halt_Instruction));
  or or_2 (out_9, demultiplexer_5_out0, demultiplexer_4_out0);
  Demultiplexer demultiplexer_5 (
    .out0(demultiplexer_5_out0), .out1(demultiplexer_5_out1), .in(out_9), .en(Ejecutada));  // open: sel
  or or_3 (CS, undriven, undriven_2);

  // Other names for the same wires on the sheet: Clock_cambiar_etiqueta_al_nombre_real_del_reloj_que_controla_el_funcionamiento_general = in_5;
  //   Reset_cambiar_etiqueta_al_nombre_real_que_se_reciba = in_6

  // Notes on the sheet:
  //   Iddle
  //   Idle
  //   Inputs
  //   Capturar Instruccion
  //   Esquema de guia
  //   Execute
  //   Captura Instruccion
  //   Ejecuta Instruccion 
  //   End
endmodule
